# Fritzing sketch Module 2 (saved by Fritzing 0.9.3b)
breadboards: 1

parts:
  Composant1 = Arduino Uno (Rev3) - ICSP
  R2 = Resistor [tolerance=±5% resistance=220 package="0805 [SMD]"]
  R3 = Resistor [tolerance=±5% resistance=220 package="0805 [SMD]"]
  LED1 = smd LED [color="Red (633nm)" package="1206 [SMD]"]
  LED2 = smd LED [color="Red (633nm)" package="1206 [SMD]"]
  LED3 = smd LED [color="Red (633nm)" package="1206 [SMD]"]
  LED4 = smd LED [color="Red (633nm)" package="1206 [SMD]"]
  R4 = Resistor [tolerance=±5% resistance=220 package="0805 [SMD]"]
  R5 = Resistor [tolerance=±5% resistance=220 package="0805 [SMD]"]
  R6 = Resistor [tolerance=±5% resistance=220 package="0805 [SMD]"]
  R7 = Resistor [tolerance=±5% resistance=220 package="0805 [SMD]"]
  LED5 = smd LED [color="Red (633nm)" package="1206 [SMD]"]
  LED6 = smd LED [color="Red (633nm)" package="1206 [SMD]"]
  LED7 = smd LED [color="Red (633nm)" package="1206 [SMD]"]
  LED8 = smd LED [color="Red (633nm)" package="1206 [SMD]"]
  LED9 = smd LED [color="Red (633nm)" package="1206 [SMD]"]
  LED10 = smd LED [color="Red (633nm)" package="1206 [SMD]"]
  R8 = Resistor [tolerance=±5% resistance=220 package="0805 [SMD]"]
  R9 = Resistor [tolerance=±5% resistance=220 package="0805 [SMD]"]
  R10 = Resistor [tolerance=±5% resistance=220 package="0805 [SMD]"]
  R11 = Resistor [tolerance=±5% resistance=220 package="0805 [SMD]"]

nets:
  N1: Composant1.ICSP_MISO, Composant1.D12/MISO, R2.Pin_1
  N2: Composant1.D8, R7.Pin_1
  N3: Composant1.D9_PWM, R6.Pin_1
  N4: Composant1.D10_PWM/SS, R5.Pin_1
  N5: Composant1.D11_PWM/MOSI, R4.Pin_1
  N6: Composant1.D13/SCK, R3.Pin_1
  N7: Composant1.D4, R11.Pin_1
  N8: Composant1.D5_PWM, R10.Pin_1
  N9: Composant1.D6_PWM, R8.Pin_1
  N10: Composant1.D7, R9.Pin_1
  N11: Composant1.GND, LED1.anode, LED2.anode, LED3.anode, LED4.anode, LED5.anode, LED6.anode, LED7.anode, LED8.anode, LED9.anode, LED10.anode
  N12: R2.Pin_0, LED3.cathode
  N13: R3.Pin_0, LED2.cathode
  N14: LED1.cathode, R4.Pin_0
  N15: LED4.cathode, R5.Pin_0
  N16: R6.Pin_0, LED5.cathode
  N17: R7.Pin_0, LED10.cathode
  N18: LED6.cathode, R8.Pin_0
  N19: LED7.cathode, R11.Pin_0
  N20: LED8.cathode, R10.Pin_0
  N21: LED9.cathode, R9.Pin_0
